// Logisim project Circuit.circ as structural Verilog: 2 circuits, main circuit main
module main (
);

  cpu cpu_1 ();  // open: RAM_ADDR
endmodule

module cpu (
  output [15:0] RAM_ADDR
);

  wire demultiplexer_1_out0, demultiplexer_1_out1, demultiplexer_1_out2, demultiplexer_1_out3,
       demultiplexer_1_out4, demultiplexer_1_out5, demultiplexer_1_out6, demultiplexer_1_out7,
       demultiplexer_2_out0, demultiplexer_2_out1, demultiplexer_2_out2, demultiplexer_2_out3,
       demultiplexer_2_out4, demultiplexer_2_out5, demultiplexer_2_out6, demultiplexer_2_out7,
       demultiplexer_2_out8, demultiplexer_2_out9, demultiplexer_2_out10, demultiplexer_2_out11,
       demultiplexer_2_out12, demultiplexer_2_out13, demultiplexer_2_out14, demultiplexer_2_out15, or_1_out,
       or_2_out, or_3_out, or_4_out, or_5_out, or_6_out, or_7_out, or_8_out, or_9_out, or_10_out, or_11_out,
       or_12_out, or_13_out, or_14_out, or_15_out, or_16_out, undriven_2, undriven_3, undriven_4, undriven_5;
  wire [7:0] multiplexer_3_out, multiplexer_4_out, register_14_q;
  wire [15:0] multiplexer_1_out, multiplexer_2_out, ProgramCounter_q, register_2_q, register_4_q,
       register_6_q, register_8_q, register_10_q, register_12_q, register_16_q, undriven;
  wire [15:8] register_13_q;

  Demultiplexer #(.select(3)) demultiplexer_1 (
    .out0(demultiplexer_1_out0), .out1(demultiplexer_1_out1), .out2(demultiplexer_1_out2),
    .out3(demultiplexer_1_out3), .out4(demultiplexer_1_out4), .out5(demultiplexer_1_out5),
    .out6(demultiplexer_1_out6), .out7(demultiplexer_1_out7), .in(undriven_2));  // open: sel
  Demultiplexer #(.select(4)) demultiplexer_2 (
    .out0(demultiplexer_2_out0), .out1(demultiplexer_2_out1), .out2(demultiplexer_2_out2),
    .out3(demultiplexer_2_out3), .out4(demultiplexer_2_out4), .out5(demultiplexer_2_out5),
    .out6(demultiplexer_2_out6), .out7(demultiplexer_2_out7), .out8(demultiplexer_2_out8),
    .out9(demultiplexer_2_out9), .out10(demultiplexer_2_out10), .out11(demultiplexer_2_out11),
    .out12(demultiplexer_2_out12), .out13(demultiplexer_2_out13), .out14(demultiplexer_2_out14),
    .out15(demultiplexer_2_out15), .in(undriven_3));  // open: sel
  or or_1 (or_1_out, demultiplexer_1_out0, demultiplexer_2_out0);
  or or_2 (or_2_out, demultiplexer_1_out0, demultiplexer_2_out1);
  or or_3 (or_3_out, demultiplexer_1_out1, demultiplexer_2_out2);
  or or_4 (or_4_out, demultiplexer_1_out1, demultiplexer_2_out3);
  or or_5 (or_5_out, demultiplexer_1_out2, demultiplexer_2_out4);
  or or_6 (or_6_out, demultiplexer_1_out2, demultiplexer_2_out5);
  or or_7 (or_7_out, demultiplexer_1_out3, demultiplexer_2_out6);
  or or_8 (or_8_out, demultiplexer_1_out3, demultiplexer_2_out7);
  or or_9 (or_9_out, demultiplexer_1_out4, demultiplexer_2_out8);
  or or_10 (or_10_out, demultiplexer_1_out4, demultiplexer_2_out9);
  or or_11 (or_11_out, demultiplexer_1_out5, demultiplexer_2_out10);
  or or_12 (or_12_out, demultiplexer_1_out5, demultiplexer_2_out11);
  or or_13 (or_13_out, demultiplexer_1_out6, demultiplexer_2_out12);
  or or_14 (or_14_out, demultiplexer_1_out6, demultiplexer_2_out13);
  or or_15 (or_15_out, demultiplexer_1_out7, demultiplexer_2_out14);
  or or_16 (or_16_out, demultiplexer_1_out7, demultiplexer_2_out15);
  Counter #(.max('hffff), .width(16)) ProgramCounter (.Q(ProgramCounter_q));  // open: clr, load, up, count, clk, D, carry
  Register register_1 (.D(undriven[15:8]), .en(or_1_out), .clk(undriven_4), .Q(register_2_q[15:8]));  // open: clr
  Register register_2 (.D(undriven[7:0]), .en(or_2_out), .clk(undriven_4), .Q(register_2_q[7:0]));  // open: clr
  Register register_3 (.D(undriven[15:8]), .en(or_3_out), .clk(undriven_4), .Q(register_4_q[15:8]));  // open: clr
  Register register_4 (.en(or_4_out), .clk(undriven_4), .Q(register_4_q[7:0]));  // open: D, clr
  Register register_5 (.D(undriven[15:8]), .en(or_5_out), .clk(undriven_4), .Q(register_6_q[15:8]));  // open: clr
  Register register_6 (.D(undriven[7:0]), .en(or_6_out), .clk(undriven_4), .Q(register_6_q[7:0]));  // open: clr
  Register register_7 (.D(undriven[15:8]), .en(or_7_out), .clk(undriven_4), .Q(register_8_q[15:8]));  // open: clr
  Register register_8 (.D(undriven[7:0]), .en(or_8_out), .clk(undriven_4), .Q(register_8_q[7:0]));  // open: clr
  Register register_9 (.D(undriven[15:8]), .en(or_9_out), .clk(undriven_4), .Q(register_10_q[15:8]));  // open: clr
  Register register_10 (.D(undriven[7:0]), .en(or_10_out), .clk(undriven_4), .Q(register_10_q[7:0]));  // open: clr
  Register register_11 (.D(undriven[15:8]), .en(or_11_out), .clk(undriven_4), .Q(register_12_q[15:8]));  // open: clr
  Register register_12 (.D(undriven[7:0]), .en(or_12_out), .clk(undriven_4), .Q(register_12_q[7:0]));  // open: clr
  Register register_13 (.D(undriven[15:8]), .en(or_13_out), .clk(undriven_4), .Q(register_13_q));  // open: clr
  Register register_14 (.D(undriven[7:0]), .en(or_14_out), .clk(undriven_4), .Q(register_14_q));  // open: clr
  Register register_15 (.D(undriven[15:8]), .en(or_15_out), .clk(undriven_4), .Q(register_16_q[15:8]));  // open: clr
  Register register_16 (.D(undriven[7:0]), .en(or_16_out), .clk(undriven_4), .Q(register_16_q[7:0]));  // open: clr
  assign RAM_ADDR = undriven_5 ? ProgramCounter_q : 16'bz;  // Controlled_Buffer controlled_buffer_1
  Multiplexer #(.select(3), .width(16)) multiplexer_1 (
    .in0(register_2_q), .in1(register_4_q), .in2(register_6_q), .in3(register_8_q), .in4(register_10_q),
    .in5(register_12_q), .in6({register_13_q, register_14_q}), .in7(register_16_q), .out(multiplexer_1_out));  // open: sel
  Multiplexer #(.select(3), .width(16)) multiplexer_2 (
    .in0(register_2_q), .in1(register_4_q), .in2(register_6_q), .in3(register_8_q), .in4(register_10_q),
    .in5(register_12_q), .in6({register_13_q, register_14_q}), .in7(register_16_q), .out(multiplexer_2_out));  // open: sel
  Multiplexer #(.select(4), .width(8)) multiplexer_3 (
    .in0(register_2_q[15:8]), .in1(register_2_q[7:0]), .in2(register_4_q[15:8]), .in3(register_4_q[7:0]),
    .in4(register_6_q[15:8]), .in5(register_6_q[7:0]), .in6(register_8_q[15:8]), .in7(register_8_q[7:0]),
    .in8(register_10_q[15:8]), .in9(register_10_q[7:0]), .in10(register_12_q[15:8]),
    .in11(register_12_q[7:0]), .in12(register_13_q), .in13(register_14_q), .in14(register_16_q[15:8]),
    .in15(register_16_q[7:0]), .out(multiplexer_3_out));  // open: sel
  Multiplexer #(.select(4), .width(8)) multiplexer_4 (
    .in0(register_2_q[15:8]), .in1(register_2_q[7:0]), .in2(register_4_q[15:8]), .in3(register_4_q[7:0]),
    .in4(register_6_q[15:8]), .in5(register_6_q[7:0]), .in6(register_8_q[15:8]), .in7(register_8_q[7:0]),
    .in8(register_10_q[15:8]), .in9(register_10_q[7:0]), .in10(register_12_q[15:8]),
    .in11(register_12_q[7:0]), .in12(register_13_q), .in13(register_14_q), .in14(register_16_q[15:8]),
    .in15(register_16_q[7:0]), .out(multiplexer_4_out));  // open: sel
  Register #(.width(16)) CurInstr ();  // open: D, en, clk, Q, clr

  // Notes on the sheet:
  //   Registers, r1-16
  //   8 bit but can be combined
endmodule
